// Logisim project sram_16bytes.circ as structural Verilog: 3 circuits, main circuit sram_16_bytes
module sram_16_bytes (
  input  O7,
  input  O6,
  input  O5,
  input  O4,
  input  O3,
  input  O2,
  input  O1,
  input  O0,
  input  I7,
  input  I6,
  input  I5,
  input  I4,
  input  I3,
  input  I2,
  input  I1,
  input  I0,
  input  Read,
  input  Write,
  input  Clear,
  input  clock,
  input  A3,
  input  A2,
  input  A1,
  input  A0,
  input  in_25,
  output D7,
  output D6,
  output D5,
  output D4,
  output D3,
  output D2,
  output D1,
  output D0
);

  wire and_1_out, and_2_out, and_3_out, and_4_out, and_5_out, and_6_out, and_7_out, and_8_out, and_9_out,
       and_10_out, and_11_out, and_12_out, and_13_out, and_14_out, and_15_out, and_16_out,
       controlled_buffer_9_out, controlled_buffer_10_out, controlled_buffer_11_out, controlled_buffer_12_out,
       controlled_buffer_13_out, controlled_buffer_14_out, controlled_buffer_15_out,
       controlled_buffer_16_out, decoder_4bits_1_d0, decoder_4bits_1_d1, decoder_4bits_1_d2,
       decoder_4bits_1_d4, decoder_4bits_1_d5, decoder_4bits_1_d6, decoder_4bits_1_d7, decoder_4bits_1_d8,
       decoder_4bits_1_d9, decoder_4bits_1_da, decoder_4bits_1_db, decoder_4bits_1_dc, decoder_4bits_1_dd,
       decoder_4bits_1_de, decoder_4bits_1_df, register8_bits_1_b0, register8_bits_1_b1, register8_bits_1_b2,
       register8_bits_1_b3, register8_bits_1_b4, register8_bits_1_b5, register8_bits_1_b6,
       register8_bits_1_b7, register8_bits_2_b0, register8_bits_2_b1, register8_bits_2_b2,
       register8_bits_2_b3, register8_bits_2_b4, register8_bits_2_b5, register8_bits_2_b6,
       register8_bits_2_b7, register8_bits_3_b0, register8_bits_3_b1, register8_bits_3_b2,
       register8_bits_3_b3, register8_bits_3_b4, register8_bits_3_b5, register8_bits_3_b6,
       register8_bits_3_b7, register8_bits_4_b0, register8_bits_4_b1, register8_bits_4_b2,
       register8_bits_4_b3, register8_bits_4_b4, register8_bits_4_b5, register8_bits_4_b6,
       register8_bits_4_b7, register8_bits_5_b0, register8_bits_5_b1, register8_bits_5_b2,
       register8_bits_5_b3, register8_bits_5_b4, register8_bits_5_b5, register8_bits_5_b6,
       register8_bits_5_b7, register8_bits_6_b0, register8_bits_6_b1, register8_bits_6_b2,
       register8_bits_6_b3, register8_bits_6_b4, register8_bits_6_b5, register8_bits_6_b6,
       register8_bits_6_b7, register8_bits_7_b0, register8_bits_7_b1, register8_bits_7_b2,
       register8_bits_7_b3, register8_bits_7_b4, register8_bits_7_b5, register8_bits_7_b6,
       register8_bits_7_b7, register8_bits_8_b0, register8_bits_8_b1, register8_bits_8_b2,
       register8_bits_8_b3, register8_bits_8_b4, register8_bits_8_b5, register8_bits_8_b6,
       register8_bits_8_b7, register8_bits_9_b0, register8_bits_9_b1, register8_bits_9_b2,
       register8_bits_9_b3, register8_bits_9_b4, register8_bits_9_b5, register8_bits_9_b6,
       register8_bits_9_b7, register8_bits_10_b0, register8_bits_10_b1, register8_bits_10_b2,
       register8_bits_10_b3, register8_bits_10_b4, register8_bits_10_b5, register8_bits_10_b6,
       register8_bits_10_b7, register8_bits_11_b0, register8_bits_11_b1, register8_bits_11_b2,
       register8_bits_11_b3, register8_bits_11_b4, register8_bits_11_b5, register8_bits_11_b6,
       register8_bits_11_b7, register8_bits_12_b0, register8_bits_12_b1, register8_bits_12_b2,
       register8_bits_12_b3, register8_bits_12_b5, register8_bits_12_b6, register8_bits_12_b7,
       register8_bits_13_b0, register8_bits_13_b1, register8_bits_13_b2, register8_bits_13_b3,
       register8_bits_13_b4, register8_bits_13_b5, register8_bits_13_b6, register8_bits_13_b7,
       register8_bits_14_b0, register8_bits_14_b1, register8_bits_14_b2, register8_bits_14_b3,
       register8_bits_14_b4, register8_bits_14_b5, register8_bits_14_b6, register8_bits_14_b7,
       register8_bits_15_b0, register8_bits_15_b1, register8_bits_15_b2, register8_bits_15_b3,
       register8_bits_15_b4, register8_bits_15_b5, register8_bits_15_b7, register8_bits_16_b0,
       register8_bits_16_b1, register8_bits_16_b2, register8_bits_16_b3, register8_bits_16_b4,
       register8_bits_16_b5, register8_bits_16_b6, register8_bits_16_b7, undriven;

  decoder_4bits decoder_4bits_1 (
    .A3(A3), .A2(A2), .A1(A1), .A0(A0), .Enable(in_25), .DF(decoder_4bits_1_df), .DE(decoder_4bits_1_de),
    .DD(decoder_4bits_1_dd), .DC(decoder_4bits_1_dc), .DB(decoder_4bits_1_db), .DA(decoder_4bits_1_da),
    .D9(decoder_4bits_1_d9), .D8(decoder_4bits_1_d8), .D7(decoder_4bits_1_d7), .D6(decoder_4bits_1_d6),
    .D5(decoder_4bits_1_d5), .D4(decoder_4bits_1_d4), .D3(decoder_4bits_1_dd), .D2(decoder_4bits_1_d2),
    .D1(decoder_4bits_1_d1), .D0(decoder_4bits_1_d0));
  and and_1 (and_1_out, decoder_4bits_1_df, Write);
  and and_2 (and_2_out, decoder_4bits_1_de, Write);
  and and_3 (and_3_out, decoder_4bits_1_dd, undriven);
  and and_4 (and_4_out, decoder_4bits_1_dc, undriven);
  and and_5 (and_5_out, decoder_4bits_1_db, undriven);
  and and_6 (and_6_out, decoder_4bits_1_da, undriven);
  and and_7 (and_7_out, decoder_4bits_1_d9, undriven);
  and and_8 (and_8_out, decoder_4bits_1_d8, undriven);
  register8_bits register8_bits_1 (
    .I2(controlled_buffer_14_out), .I1(controlled_buffer_15_out), .I6(controlled_buffer_10_out),
    .I5(controlled_buffer_11_out), .I4(controlled_buffer_12_out), .I3(controlled_buffer_13_out),
    .I0(controlled_buffer_16_out), .I7(controlled_buffer_9_out), .Clock(clock), .Load(and_8_out),
    .Reset(Clear), .Enable(decoder_4bits_1_d8), .B7(register8_bits_1_b7), .D07(D7), .B6(register8_bits_1_b6),
    .D06(D6), .B5(register8_bits_1_b5), .D05(D5), .B4(register8_bits_1_b4), .D04(D4),
    .B3(register8_bits_1_b3), .D03(D3), .B2(register8_bits_1_b2), .D02(D2), .B1(register8_bits_1_b1),
    .D01(D1), .B0(register8_bits_1_b0), .D00(D0));
  register8_bits register8_bits_2 (
    .I2(controlled_buffer_14_out), .I1(controlled_buffer_15_out), .I6(controlled_buffer_10_out),
    .I5(controlled_buffer_11_out), .I4(controlled_buffer_12_out), .I3(controlled_buffer_13_out),
    .I0(controlled_buffer_16_out), .I7(controlled_buffer_9_out), .Clock(clock), .Load(and_1_out),
    .Reset(Clear), .Enable(decoder_4bits_1_df), .B7(register8_bits_2_b7), .D07(D7), .B6(register8_bits_2_b6),
    .D06(D6), .B5(register8_bits_2_b5), .D05(D5), .B4(register8_bits_2_b4), .D04(D4),
    .B3(register8_bits_2_b3), .D03(D3), .B2(register8_bits_2_b2), .D02(D2), .B1(register8_bits_2_b1),
    .D01(D1), .B0(register8_bits_2_b0), .D00(D0));
  register8_bits register8_bits_3 (
    .I2(controlled_buffer_14_out), .I1(controlled_buffer_15_out), .I6(controlled_buffer_10_out),
    .I5(controlled_buffer_11_out), .I4(controlled_buffer_12_out), .I3(controlled_buffer_13_out),
    .I0(controlled_buffer_16_out), .I7(controlled_buffer_9_out), .Clock(clock), .Load(and_2_out),
    .Reset(Clear), .Enable(decoder_4bits_1_de), .B7(register8_bits_3_b7), .D07(D7), .B6(register8_bits_3_b6),
    .D06(D6), .B5(register8_bits_3_b5), .D05(D5), .B4(register8_bits_3_b4), .D04(D4),
    .B3(register8_bits_3_b3), .D03(D3), .B2(register8_bits_3_b2), .D02(D2), .B1(register8_bits_3_b1),
    .D01(D1), .B0(register8_bits_3_b0), .D00(D0));
  register8_bits register8_bits_4 (
    .I2(controlled_buffer_14_out), .I1(controlled_buffer_15_out), .I6(controlled_buffer_10_out),
    .I5(controlled_buffer_11_out), .I4(controlled_buffer_12_out), .I3(controlled_buffer_13_out),
    .I0(controlled_buffer_16_out), .I7(controlled_buffer_9_out), .Clock(clock), .Load(and_3_out),
    .Reset(Clear), .Enable(decoder_4bits_1_dd), .B7(register8_bits_4_b7), .D07(D7), .B6(register8_bits_4_b6),
    .D06(D6), .B5(register8_bits_4_b5), .D05(D5), .B4(register8_bits_4_b4), .D04(D4),
    .B3(register8_bits_4_b3), .D03(D3), .B2(register8_bits_4_b2), .D02(D2), .B1(register8_bits_4_b1),
    .D01(D1), .B0(register8_bits_4_b0), .D00(D0));
  register8_bits register8_bits_5 (
    .I2(controlled_buffer_14_out), .I1(controlled_buffer_15_out), .I6(controlled_buffer_10_out),
    .I5(controlled_buffer_11_out), .I4(controlled_buffer_12_out), .I3(controlled_buffer_13_out),
    .I0(controlled_buffer_16_out), .I7(controlled_buffer_9_out), .Clock(clock), .Load(and_4_out),
    .Reset(Clear), .Enable(decoder_4bits_1_dc), .B7(register8_bits_5_b7), .D07(D7), .B6(register8_bits_5_b6),
    .D06(D6), .B5(register8_bits_5_b5), .D05(D5), .B4(register8_bits_5_b4), .D04(D4),
    .B3(register8_bits_5_b3), .D03(D3), .B2(register8_bits_5_b2), .D02(D2), .B1(register8_bits_5_b1),
    .D01(D1), .B0(register8_bits_5_b0), .D00(D0));
  register8_bits register8_bits_6 (
    .I2(controlled_buffer_14_out), .I1(controlled_buffer_15_out), .I6(controlled_buffer_10_out),
    .I5(controlled_buffer_11_out), .I4(controlled_buffer_12_out), .I3(controlled_buffer_13_out),
    .I0(controlled_buffer_16_out), .I7(controlled_buffer_9_out), .Clock(clock), .Load(and_5_out),
    .Reset(Clear), .Enable(decoder_4bits_1_db), .B7(register8_bits_6_b7), .D07(D7), .B6(register8_bits_6_b6),
    .D06(D6), .B5(register8_bits_6_b5), .D05(D5), .B4(register8_bits_6_b4), .D04(D4),
    .B3(register8_bits_6_b3), .D03(D3), .B2(register8_bits_6_b2), .D02(D2), .B1(register8_bits_6_b1),
    .D01(D1), .B0(register8_bits_6_b0), .D00(D0));
  register8_bits register8_bits_7 (
    .I2(controlled_buffer_14_out), .I1(controlled_buffer_15_out), .I6(controlled_buffer_10_out),
    .I5(controlled_buffer_11_out), .I4(controlled_buffer_12_out), .I3(controlled_buffer_13_out),
    .I0(controlled_buffer_16_out), .I7(controlled_buffer_9_out), .Clock(clock), .Load(and_6_out),
    .Reset(Clear), .Enable(decoder_4bits_1_da), .B7(register8_bits_7_b7), .D07(D7), .B6(register8_bits_7_b6),
    .D06(D6), .B5(register8_bits_7_b5), .D05(D5), .B4(register8_bits_7_b4), .D04(D4),
    .B3(register8_bits_7_b3), .D03(D3), .B2(register8_bits_7_b2), .D02(D2), .B1(register8_bits_7_b1),
    .D01(D1), .B0(register8_bits_7_b0), .D00(D0));
  register8_bits register8_bits_8 (
    .I2(controlled_buffer_14_out), .I1(controlled_buffer_15_out), .I6(controlled_buffer_10_out),
    .I5(controlled_buffer_11_out), .I4(controlled_buffer_12_out), .I3(controlled_buffer_13_out),
    .I0(controlled_buffer_16_out), .I7(controlled_buffer_9_out), .Clock(clock), .Load(and_7_out),
    .Reset(Clear), .Enable(decoder_4bits_1_d9), .B7(register8_bits_8_b7), .D07(D7), .B6(register8_bits_8_b6),
    .D06(D6), .B5(register8_bits_8_b5), .D05(D5), .B4(register8_bits_8_b4), .D04(D4),
    .B3(register8_bits_8_b3), .D03(D3), .B2(register8_bits_8_b2), .D02(D2), .B1(register8_bits_8_b1),
    .D01(D1), .B0(register8_bits_8_b0), .D00(D0));
  assign O7 = Read ? D7 : 1'bz;  // Controlled_Buffer controlled_buffer_1
  assign O6 = Read ? D6 : 1'bz;  // Controlled_Buffer controlled_buffer_2
  DotMatrix #(.dotshape("circle"), .inputtype("row"), .matrixcols(1), .matrixrows(8)) dotmatrix_1 (
    .row0(register8_bits_2_b7), .row1(register8_bits_2_b6), .row2(register8_bits_2_b5),
    .row3(register8_bits_2_b4), .row4(register8_bits_2_b3), .row5(register8_bits_2_b2),
    .row6(register8_bits_2_b1), .row7(register8_bits_2_b0));
  DotMatrix #(.dotshape("circle"), .inputtype("row"), .matrixcols(1), .matrixrows(8)) dotmatrix_2 (
    .row0(register8_bits_3_b7), .row1(register8_bits_3_b6), .row2(register8_bits_3_b5),
    .row3(register8_bits_3_b4), .row4(register8_bits_3_b3), .row5(register8_bits_3_b2),
    .row6(register8_bits_3_b1), .row7(register8_bits_3_b0));
  DotMatrix #(.dotshape("circle"), .inputtype("row"), .matrixcols(1), .matrixrows(8)) dotmatrix_3 (
    .row0(register8_bits_4_b7), .row1(register8_bits_4_b6), .row2(register8_bits_4_b5),
    .row3(register8_bits_4_b4), .row4(register8_bits_4_b3), .row5(register8_bits_4_b2),
    .row6(register8_bits_4_b1), .row7(register8_bits_4_b0));
  DotMatrix #(.dotshape("circle"), .inputtype("row"), .matrixcols(1), .matrixrows(8)) dotmatrix_4 (
    .row0(register8_bits_5_b7), .row1(register8_bits_5_b6), .row2(register8_bits_5_b5),
    .row3(register8_bits_5_b4), .row4(register8_bits_5_b3), .row5(register8_bits_5_b2),
    .row6(register8_bits_5_b1), .row7(register8_bits_5_b0));
  DotMatrix #(.dotshape("circle"), .inputtype("row"), .matrixcols(1), .matrixrows(8)) dotmatrix_5 (
    .row0(register8_bits_6_b7), .row1(register8_bits_6_b6), .row2(register8_bits_6_b5),
    .row3(register8_bits_6_b4), .row4(register8_bits_6_b3), .row5(register8_bits_6_b2),
    .row6(register8_bits_6_b1), .row7(register8_bits_6_b0));
  DotMatrix #(.dotshape("circle"), .inputtype("row"), .matrixcols(1), .matrixrows(8)) dotmatrix_6 (
    .row0(register8_bits_7_b7), .row1(register8_bits_7_b6), .row2(register8_bits_7_b5),
    .row3(register8_bits_7_b4), .row4(register8_bits_7_b3), .row5(register8_bits_7_b2),
    .row6(register8_bits_7_b1), .row7(register8_bits_7_b0));
  DotMatrix #(.dotshape("circle"), .inputtype("row"), .matrixcols(1), .matrixrows(8)) dotmatrix_7 (
    .row0(register8_bits_8_b7), .row1(register8_bits_8_b6), .row2(register8_bits_8_b5),
    .row3(register8_bits_8_b4), .row4(register8_bits_8_b3), .row5(register8_bits_8_b2),
    .row6(register8_bits_8_b1), .row7(register8_bits_8_b0));
  DotMatrix #(.dotshape("circle"), .inputtype("row"), .matrixcols(1), .matrixrows(8)) dotmatrix_8 (
    .row0(register8_bits_1_b7), .row1(register8_bits_1_b6), .row2(register8_bits_1_b5),
    .row3(register8_bits_1_b4), .row4(register8_bits_1_b3), .row5(register8_bits_1_b2),
    .row6(register8_bits_1_b1), .row7(register8_bits_1_b0));
  assign O5 = Read ? D5 : 1'bz;  // Controlled_Buffer controlled_buffer_3
  assign O4 = Read ? D4 : 1'bz;  // Controlled_Buffer controlled_buffer_4
  assign O3 = Read ? D3 : 1'bz;  // Controlled_Buffer controlled_buffer_5
  assign O2 = Read ? D2 : 1'bz;  // Controlled_Buffer controlled_buffer_6
  assign O1 = Read ? D1 : 1'bz;  // Controlled_Buffer controlled_buffer_7
  assign O0 = Read ? D0 : 1'bz;  // Controlled_Buffer controlled_buffer_8
  assign controlled_buffer_9_out = Write ? I7 : 1'bz;  // Controlled_Buffer controlled_buffer_9
  assign controlled_buffer_10_out = Write ? I6 : 1'bz;  // Controlled_Buffer controlled_buffer_10
  assign controlled_buffer_11_out = Write ? I5 : 1'bz;  // Controlled_Buffer controlled_buffer_11
  assign controlled_buffer_12_out = Write ? I4 : 1'bz;  // Controlled_Buffer controlled_buffer_12
  assign controlled_buffer_13_out = Write ? I3 : 1'bz;  // Controlled_Buffer controlled_buffer_13
  assign controlled_buffer_14_out = Write ? I2 : 1'bz;  // Controlled_Buffer controlled_buffer_14
  assign controlled_buffer_15_out = Write ? I1 : 1'bz;  // Controlled_Buffer controlled_buffer_15
  register8_bits register8_bits_9 (
    .I2(controlled_buffer_14_out), .I1(controlled_buffer_15_out), .I6(controlled_buffer_10_out),
    .I5(controlled_buffer_11_out), .I4(controlled_buffer_12_out), .I3(controlled_buffer_13_out),
    .I0(controlled_buffer_16_out), .I7(controlled_buffer_9_out), .Clock(clock), .Load(and_15_out),
    .Reset(Clear), .Enable(decoder_4bits_1_d6), .B7(register8_bits_9_b7), .D07(D7), .B6(register8_bits_9_b6),
    .D06(D6), .B5(register8_bits_9_b5), .D05(D5), .B4(register8_bits_9_b4), .D04(D4),
    .B3(register8_bits_9_b3), .D03(D3), .B2(register8_bits_9_b2), .D02(D2), .B1(register8_bits_9_b1),
    .D01(D1), .B0(register8_bits_9_b0), .D00(D0));
  register8_bits register8_bits_10 (
    .I2(controlled_buffer_14_out), .I1(controlled_buffer_15_out), .I6(controlled_buffer_10_out),
    .I5(controlled_buffer_11_out), .I4(controlled_buffer_12_out), .I3(controlled_buffer_13_out),
    .I0(controlled_buffer_16_out), .I7(controlled_buffer_9_out), .Clock(clock), .Load(and_16_out),
    .Reset(Clear), .Enable(decoder_4bits_1_d7), .B7(register8_bits_10_b7), .D07(D7),
    .B6(register8_bits_10_b6), .D06(D6), .B5(register8_bits_10_b5), .D05(D5), .B4(register8_bits_10_b4),
    .D04(D4), .B3(register8_bits_10_b3), .D03(D3), .B2(register8_bits_10_b2), .D02(D2),
    .B1(register8_bits_10_b1), .D01(D1), .B0(register8_bits_10_b0), .D00(D0));
  assign controlled_buffer_16_out = Write ? I0 : 1'bz;  // Controlled_Buffer controlled_buffer_16
  register8_bits register8_bits_11 (
    .I2(controlled_buffer_14_out), .I1(controlled_buffer_15_out), .I6(controlled_buffer_10_out),
    .I5(controlled_buffer_11_out), .I4(controlled_buffer_12_out), .I3(controlled_buffer_13_out),
    .I0(controlled_buffer_16_out), .I7(controlled_buffer_9_out), .Clock(clock), .Load(and_12_out),
    .Reset(Clear), .Enable(decoder_4bits_1_d0), .B7(register8_bits_11_b7), .D07(D7),
    .B6(register8_bits_11_b6), .D06(D6), .B5(register8_bits_11_b5), .D05(D5), .B4(register8_bits_11_b4),
    .D04(D4), .B3(register8_bits_11_b3), .D03(D3), .B2(register8_bits_11_b2), .D02(D2),
    .B1(register8_bits_11_b1), .D01(D1), .B0(register8_bits_11_b0), .D00(D0));
  register8_bits register8_bits_12 (
    .I2(controlled_buffer_14_out), .I1(controlled_buffer_15_out), .I6(controlled_buffer_10_out),
    .I5(controlled_buffer_11_out), .I4(controlled_buffer_12_out), .I3(controlled_buffer_13_out),
    .I0(controlled_buffer_16_out), .I7(controlled_buffer_9_out), .Clock(clock), .Load(and_13_out),
    .Reset(Clear), .Enable(decoder_4bits_1_d1), .B7(register8_bits_12_b7), .D07(D7),
    .B6(register8_bits_12_b6), .D06(D6), .B5(register8_bits_12_b5), .D05(D5), .B4(register8_bits_12_b5),
    .D04(D4), .B3(register8_bits_12_b3), .D03(D3), .B2(register8_bits_12_b2), .D02(D2),
    .B1(register8_bits_12_b1), .D01(D1), .B0(register8_bits_12_b0), .D00(D0));
  register8_bits register8_bits_13 (
    .I2(controlled_buffer_14_out), .I1(controlled_buffer_15_out), .I6(controlled_buffer_10_out),
    .I5(controlled_buffer_11_out), .I4(controlled_buffer_12_out), .I3(controlled_buffer_13_out),
    .I0(controlled_buffer_16_out), .I7(controlled_buffer_9_out), .Clock(clock), .Load(and_14_out),
    .Reset(Clear), .Enable(decoder_4bits_1_d2), .B7(register8_bits_13_b7), .D07(D7),
    .B6(register8_bits_13_b6), .D06(D6), .B5(register8_bits_13_b5), .D05(D5), .B4(register8_bits_13_b4),
    .D04(D4), .B3(register8_bits_13_b3), .D03(D3), .B2(register8_bits_13_b2), .D02(D2),
    .B1(register8_bits_13_b1), .D01(D1), .B0(register8_bits_13_b0), .D00(D0));
  register8_bits register8_bits_14 (
    .I2(controlled_buffer_14_out), .I1(controlled_buffer_15_out), .I6(controlled_buffer_10_out),
    .I5(controlled_buffer_11_out), .I4(controlled_buffer_12_out), .I3(controlled_buffer_13_out),
    .I0(controlled_buffer_16_out), .I7(controlled_buffer_9_out), .Clock(clock), .Load(and_9_out),
    .Reset(Clear), .Enable(decoder_4bits_1_dd), .B7(register8_bits_14_b7), .D07(D7),
    .B6(register8_bits_14_b6), .D06(D6), .B5(register8_bits_14_b5), .D05(D5), .B4(register8_bits_14_b4),
    .D04(D4), .B3(register8_bits_14_b3), .D03(D3), .B2(register8_bits_14_b2), .D02(D2),
    .B1(register8_bits_14_b1), .D01(D1), .B0(register8_bits_14_b0), .D00(D0));
  register8_bits register8_bits_15 (
    .I2(controlled_buffer_14_out), .I1(controlled_buffer_15_out), .I6(controlled_buffer_10_out),
    .I5(controlled_buffer_11_out), .I4(controlled_buffer_12_out), .I3(controlled_buffer_13_out),
    .I0(controlled_buffer_16_out), .I7(controlled_buffer_9_out), .Clock(clock), .Load(and_10_out),
    .Reset(Clear), .Enable(decoder_4bits_1_d4), .B7(register8_bits_15_b7), .D07(D7),
    .B6(register8_bits_15_b7), .D06(D6), .B5(register8_bits_15_b5), .D05(D5), .B4(register8_bits_15_b4),
    .D04(D4), .B3(register8_bits_15_b3), .D03(D3), .B2(register8_bits_15_b2), .D02(D2),
    .B1(register8_bits_15_b1), .D01(D1), .B0(register8_bits_15_b0), .D00(D0));
  register8_bits register8_bits_16 (
    .I2(controlled_buffer_14_out), .I1(controlled_buffer_15_out), .I6(controlled_buffer_10_out),
    .I5(controlled_buffer_11_out), .I4(controlled_buffer_12_out), .I3(controlled_buffer_13_out),
    .I0(controlled_buffer_16_out), .I7(controlled_buffer_9_out), .Clock(clock), .Load(and_11_out),
    .Reset(Clear), .Enable(decoder_4bits_1_d5), .B7(register8_bits_16_b7), .D07(D7),
    .B6(register8_bits_16_b6), .D06(D6), .B5(register8_bits_16_b5), .D05(D5), .B4(register8_bits_16_b4),
    .D04(D4), .B3(register8_bits_16_b3), .D03(D3), .B2(register8_bits_16_b2), .D02(D2),
    .B1(register8_bits_16_b1), .D01(D1), .B0(register8_bits_16_b0), .D00(D0));
  and and_9 (and_9_out, and_13_out, decoder_4bits_1_dd);
  and and_10 (and_10_out, and_13_out, decoder_4bits_1_d4);
  and and_11 (and_11_out, and_13_out, decoder_4bits_1_d5);
  DotMatrix #(.dotshape("circle"), .inputtype("row"), .matrixcols(1), .matrixrows(8)) dotmatrix_9 (
    .row0(register8_bits_11_b7), .row1(register8_bits_11_b6), .row2(register8_bits_11_b5),
    .row3(register8_bits_11_b4), .row4(register8_bits_11_b3), .row5(register8_bits_11_b2),
    .row6(register8_bits_11_b1), .row7(register8_bits_11_b0));
  and and_12 (and_12_out, Write, decoder_4bits_1_d0);
  DotMatrix #(.dotshape("circle"), .inputtype("row"), .matrixcols(1), .matrixrows(8)) dotmatrix_10 (
    .row0(register8_bits_12_b7), .row1(register8_bits_12_b6), .row2(register8_bits_12_b5),
    .row3(register8_bits_12_b5), .row4(register8_bits_12_b3), .row5(register8_bits_12_b2),
    .row6(register8_bits_12_b1), .row7(register8_bits_12_b0));
  and and_13 (and_13_out, Write, decoder_4bits_1_d1);
  DotMatrix #(.dotshape("circle"), .inputtype("row"), .matrixcols(1), .matrixrows(8)) dotmatrix_11 (
    .row0(register8_bits_13_b7), .row1(register8_bits_13_b6), .row2(register8_bits_13_b5),
    .row3(register8_bits_13_b4), .row4(register8_bits_13_b3), .row5(register8_bits_13_b2),
    .row6(register8_bits_13_b1), .row7(register8_bits_13_b0));
  and and_14 (and_14_out, and_13_out, decoder_4bits_1_d2);
  DotMatrix #(.dotshape("circle"), .inputtype("row"), .matrixcols(1), .matrixrows(8)) dotmatrix_12 (
    .row0(register8_bits_14_b7), .row1(register8_bits_14_b6), .row2(register8_bits_14_b5),
    .row3(register8_bits_14_b4), .row4(register8_bits_14_b3), .row5(register8_bits_14_b2),
    .row6(register8_bits_14_b1), .row7(register8_bits_14_b0));
  and and_15 (and_15_out, and_11_out, decoder_4bits_1_d6);
  DotMatrix #(.dotshape("circle"), .inputtype("row"), .matrixcols(1), .matrixrows(8)) dotmatrix_13 (
    .row0(register8_bits_10_b7), .row1(register8_bits_10_b6), .row2(register8_bits_10_b5),
    .row3(register8_bits_10_b4), .row4(register8_bits_10_b3), .row5(register8_bits_10_b2),
    .row6(register8_bits_10_b1), .row7(register8_bits_10_b0));
  and and_16 (and_16_out, and_11_out, decoder_4bits_1_d7);
  DotMatrix #(.dotshape("circle"), .inputtype("row"), .matrixcols(1), .matrixrows(8)) dotmatrix_14 (
    .row0(register8_bits_15_b7), .row1(register8_bits_15_b7), .row2(register8_bits_15_b5),
    .row3(register8_bits_15_b4), .row4(register8_bits_15_b3), .row5(register8_bits_15_b2),
    .row6(register8_bits_15_b1), .row7(register8_bits_15_b0));
  DotMatrix #(.dotshape("circle"), .inputtype("row"), .matrixcols(1), .matrixrows(8)) dotmatrix_15 (
    .row0(register8_bits_16_b7), .row1(register8_bits_16_b6), .row2(register8_bits_16_b5),
    .row3(register8_bits_16_b4), .row4(register8_bits_16_b3), .row5(register8_bits_16_b2),
    .row6(register8_bits_16_b1), .row7(register8_bits_16_b0));
  DotMatrix #(.dotshape("circle"), .inputtype("row"), .matrixcols(1), .matrixrows(8)) dotmatrix_16 (
    .row0(register8_bits_9_b7), .row1(register8_bits_9_b6), .row2(register8_bits_9_b5),
    .row3(register8_bits_9_b4), .row4(register8_bits_9_b3), .row5(register8_bits_9_b2),
    .row6(register8_bits_9_b1), .row7(register8_bits_9_b0));
endmodule

module register8_bits (
  input  I2,
  input  I1,
  input  I6,
  input  I5,
  input  I4,
  input  I3,
  input  I0,
  input  I7,
  input  Clock,
  input  Load,
  input  Reset,
  input  Enable,
  output B7,
  output D07,
  output B6,
  output D06,
  output B5,
  output D05,
  output B4,
  output D04,
  output B3,
  output D03,
  output B2,
  output D02,
  output B1,
  output D01,
  output B0,
  output D00
);

  Register #(.width(1)) register_1 (.D(I7), .en(Load), .clk(Clock), .Q(B7), .clr(Reset));
  Register #(.width(1)) register_2 (.D(I6), .en(Load), .clk(Clock), .Q(B6), .clr(Reset));
  Register #(.width(1)) register_3 (.D(I5), .en(Load), .clk(Clock), .Q(B5), .clr(Reset));
  Register #(.width(1)) register_4 (.D(I4), .en(Load), .clk(Clock), .Q(B4), .clr(Reset));
  Register #(.width(1)) register_5 (.D(I3), .en(Load), .clk(Clock), .Q(B3), .clr(Reset));
  Register #(.width(1)) register_6 (.D(I2), .en(Load), .clk(Clock), .Q(B2), .clr(Reset));
  Register #(.width(1)) register_7 (.D(I1), .en(Load), .clk(Clock), .Q(B1), .clr(Reset));
  Register #(.width(1)) register_8 (.D(I0), .en(Load), .clk(Reset), .Q(B0), .clr(Reset));
  assign D07 = Enable ? B7 : 1'bz;  // Controlled_Buffer controlled_buffer_1
  assign D06 = Enable ? B6 : 1'bz;  // Controlled_Buffer controlled_buffer_2
  assign D05 = Enable ? B5 : 1'bz;  // Controlled_Buffer controlled_buffer_3
  assign D04 = Enable ? B4 : 1'bz;  // Controlled_Buffer controlled_buffer_4
  assign D03 = Enable ? B3 : 1'bz;  // Controlled_Buffer controlled_buffer_5
  assign D02 = Enable ? B2 : 1'bz;  // Controlled_Buffer controlled_buffer_6
  assign D01 = Enable ? B1 : 1'bz;  // Controlled_Buffer controlled_buffer_7
  assign D00 = Enable ? B0 : 1'bz;  // Controlled_Buffer controlled_buffer_8
endmodule

module decoder_4bits (
  input  A3,
  input  A2,
  input  A1,
  input  A0,
  input  Enable,
  output DF,
  output DE,
  output DD,
  output DC,
  output DB,
  output DA,
  output D9,
  output D8,
  output D7,
  output D6,
  output D5,
  output D4,
  output D3,
  output D2,
  output D1,
  output D0
);

  wire and_1_out, and_2_out, and_3_out, and_4_out, and_5_out, and_6_out, and_7_out, and_8_out, and_9_out,
       and_10_out, and_11_out, and_12_out, and_13_out, and_14_out, and_15_out, and_16_out, not_1_out,
       not_2_out, not_3_out, not_4_out;

  not not_1 (not_1_out, A3);
  not not_2 (not_2_out, A2);
  not not_3 (not_3_out, A1);
  not not_4 (not_4_out, A0);
  and and_1 (and_1_out, A3, A2, A1, A0);
  assign DF = Enable ? and_1_out : 1'bz;  // Controlled_Buffer controlled_buffer_1
  and and_2 (and_2_out, A3, A2, A1, not_4_out);
  assign DE = Enable ? and_2_out : 1'bz;  // Controlled_Buffer controlled_buffer_2
  and and_3 (and_3_out, A3, A2, A0, not_3_out);
  assign DD = Enable ? and_3_out : 1'bz;  // Controlled_Buffer controlled_buffer_3
  and and_4 (and_4_out, A3, A2, not_3_out, not_4_out);
  assign DC = Enable ? and_4_out : 1'bz;  // Controlled_Buffer controlled_buffer_4
  and and_5 (and_5_out, A3, not_2_out, A1, A0);
  assign DB = Enable ? and_5_out : 1'bz;  // Controlled_Buffer controlled_buffer_5
  and and_6 (and_6_out, A3, not_2_out, A1, not_4_out);
  assign DA = Enable ? and_6_out : 1'bz;  // Controlled_Buffer controlled_buffer_6
  and and_7 (and_7_out, A3, not_2_out, not_3_out, A0);
  assign D9 = Enable ? and_7_out : 1'bz;  // Controlled_Buffer controlled_buffer_7
  and and_8 (and_8_out, A3, not_2_out, not_3_out, not_4_out);
  assign D8 = Enable ? and_8_out : 1'bz;  // Controlled_Buffer controlled_buffer_8
  and and_9 (and_9_out, not_1_out, A2, A1, A0);
  assign D7 = Enable ? and_9_out : 1'bz;  // Controlled_Buffer controlled_buffer_9
  and and_10 (and_10_out, not_4_out, A1, A2, not_1_out);
  assign D6 = Enable ? and_10_out : 1'bz;  // Controlled_Buffer controlled_buffer_10
  and and_11 (and_11_out, not_3_out, not_1_out, A2, A0);
  assign D5 = Enable ? and_11_out : 1'bz;  // Controlled_Buffer controlled_buffer_11
  and and_12 (and_12_out, not_4_out, not_3_out, A2, not_1_out);
  assign D4 = Enable ? and_12_out : 1'bz;  // Controlled_Buffer controlled_buffer_12
  and and_13 (and_13_out, not_1_out, not_2_out, A0, A1);
  assign D3 = Enable ? and_13_out : 1'bz;  // Controlled_Buffer controlled_buffer_13
  and and_14 (and_14_out, not_4_out, not_3_out, A1, not_1_out);
  assign D2 = Enable ? and_14_out : 1'bz;  // Controlled_Buffer controlled_buffer_14
  and and_15 (and_15_out, not_1_out, not_2_out, not_3_out, A0);
  assign D1 = Enable ? and_15_out : 1'bz;  // Controlled_Buffer controlled_buffer_15
  and and_16 (and_16_out, not_4_out, not_3_out, not_2_out, not_1_out);
  assign D0 = Enable ? and_16_out : 1'bz;  // Controlled_Buffer controlled_buffer_16
endmodule
